# Fritzing sketch TruckController (saved by Fritzing 0.9.3b)
circuit board: 8.46667cm x 5.64444cm
breadboards: 1

parts:
  Steering = Dagu DGServo 9g header (male) [package=THT]
  ESC = Dagu DGServo 9g header (male) [package=THT]
  Controller = RedBear-Duo
  Gearbox = Dagu DGServo 9g header (male) [package=THT]
  KingPinRelease = Dagu DGServo 9g header (male) [package=THT]

nets:
  GND: Steering.gnd, ESC.gnd, Controller.GND, Gearbox.gnd, KingPinRelease.gnd
  VCC: Steering.Vcc, ESC.Vcc, Controller.3V3, Gearbox.Vcc, KingPinRelease.Vcc
  N1: Steering.pulse, Controller.D2
  N2: ESC.pulse, Controller.D3
  N3: Controller.D0, KingPinRelease.pulse
  N4: Controller.D1, Gearbox.pulse

custom parts:
  RedBear-Duo: Duo is a thumb-size development board made to simplify the building process of Internet of Things (IoT). This part is a modification of the Particle Photon part by Brett Walach,Fabian Althaus
